# Fritzing sketch Top (saved by Fritzing 0.9.3b)
circuit board: 7.23695cm x 8.88573cm
breadboards: 1

parts:
  TO_BOTTOM = DB25M
  USB1 = USB Connectors [package=usb-a-s-nosilk]
  J = double row male pin header, 4 pins [form="♂ (male)"]
  TRS1 = Audio Jack (TRS) 3.5mm [package="4Ucon 08780 [THT]"]
  J_HOR = Basic Servo
  J_VER = Basic Servo
  CONN1 = prefix0000 [form="♂ (shrouded male)"]
  CONN2 = prefix0000 [form="♂ (shrouded male)"]
  CONN3 = prefix0000 [form="♂ (shrouded male)"]
  CONN4 = prefix0000 [form="♂ (shrouded male)"]

nets:
  GND: TO_BOTTOM.pin1, TO_BOTTOM.pin25, J_HOR.gnd, J_VER.gnd, CONN1.connector0, CONN2.connector0, CONN3.connector0, CONN4.connector0
  N1: TO_BOTTOM.pin2, J_HOR.pulse
  N2: TO_BOTTOM.pin3, J_VER.pulse
  N3: TO_BOTTOM.pin4, CONN1.connector3, CONN2.connector3, CONN3.connector3, CONN4.connector3
  N4: TO_BOTTOM.pin5, CONN1.connector2, CONN2.connector2, CONN3.connector2, CONN4.connector2
  N5: TO_BOTTOM.pin6, J.pin1
  N6: TO_BOTTOM.pin7, J.pin4
  N7: TO_BOTTOM.pin8, TRS1.Ring
  N8: TO_BOTTOM.pin9, TRS1.Tip
  VCC: TO_BOTTOM.pin14, USB1.VBUS, J_HOR.vcc, J_VER.vcc, CONN1.connector5, CONN2.connector5, CONN3.connector5, CONN4.connector5
  N9: USB1.D+, J.pin3
  N10: USB1.D-, J.pin2
  N11: USB1.GND, TRS1.Sleeve
  N12: CONN1.connector1, CONN2.connector1, CONN3.connector1, CONN4.connector1
  N13: CONN1.connector4, CONN2.connector4, CONN3.connector4, CONN4.connector4

notes:
  D-   D+
  Circuit V.0
  Top Robot
